# Fritzing sketch circuitoMain (saved by Fritzing 0.9.3b)
breadboards: 4

parts:
  U1 = 74HC595 [package="DIP16 [THT]"]
  U2 = 74HC595 [package="DIP16 [THT]"]
  U3 = 74HC595 [package="DIP16 [THT]"]
  U4 = 74HC595 [package="DIP16 [THT]"]
  U5 = 74HC595 [package="DIP16 [THT]"]
  U6 = 74HC595 [package="DIP16 [THT]"]
  U8 = 74HC595 [package="DIP16 [THT]"]

nets:
  N1: U1.Q3, U1.DS, U2.Q7
  N2: U1.Q4, U1.OE
  N3: U1.Q6, U1.SH_CP
  N4: U1.Q7, U2.SH_CP, U3.SH_CP, U4.SH_CP, U5.Q7, U6.SH_CP, U8.Q7
  GND: U1.GND, U2.GND, U2.OE, U3.OE, U4.OE, U5.GND, U6.GND, U6.OE, U8.GND
  N5: U1.Q7', U2.DS
  N6: U2.Q7', U3.DS
  VCC: U2.MR, U2.VCC, U3.MR, U3.VCC, U4.MR, U4.VCC, U6.MR, U6.VCC
  N7: U2.ST_CP, U3.ST_CP, U4.ST_CP, U6.ST_CP
  N8: U4.DS, U6.Q7'
  N9: U5.Q3, U5.DS, U6.Q7
  N10: U5.Q4, U5.OE
  N11: U5.Q6, U5.SH_CP
  N12: U5.Q7', U6.DS
  N13: U8.Q3, U8.DS
  N14: U8.Q4, U8.OE
  N15: U8.Q6, U8.SH_CP
